// Digital circuit lab04.dig as structural Verilog
module lab04 (
  input  clk,
  input  rst,
  output [31:0] PC,
  output [5:0] opcode,
  output [4:0] src1__addr,
  output [31:0] src1__out,
  output [4:0] src2__addr,
  output [31:0] src2__out,
  output [4:0] dst__addr,
  output [31:0] dst__data
);

  wire alusrc, and_1_out, mem_read, mem_write, memreg, reg_write, Regdst, u_alu_3_zero, u_control_unit_branch;
  wire [1:0] aluop;
  wire [3:0] aluc;
  wire [7:0] Alures;
  wire [15:0] cpumemory_d2;
  wire [31:0] _1D, bitextender_1_out, multiplexer_2_out, multiplexer_3_out, u_alu_2_result, u_alu_result;
  wire [31:8] u_alu_3_result;

  gen_register #(.applicationType("IVERILOG"), .CodeFile("./gen_register.v")) u_gen_register (
    .clk(clk), .rst(rst), .write_en(clk), .data_in(multiplexer_3_out), .data_out(PC));
  alu #(.applicationType("IVERILOG"), .CodeFile("./alu.v")) u_alu (
    .alu_control(4'b0010), .A(PC), .B(32'h4), .result(u_alu_result));  // open: zero
  RAMDualAccess #(.AddrBits(8), .isProgramMemory("true"), .Bits(32)) cpumemory (
    .str(mem_write), .C(clk), .ld(mem_read), .A1(Alures), .Din1(src2__out), .A2(PC[9:2]), .D1(_1D),
    .D2({opcode, src1__addr, src2__addr, cpumemory_d2}));
  BitExtender #(.inputBits(16), .outputBits(32)) bitextender_1 (.in(cpumemory_d2), .out(bitextender_1_out));
  Multiplexer #(.Bits(5)) multiplexer_1 (.sel(Regdst), .in_0(src2__addr), .in_1(cpumemory_d2[15:11]), .out(dst__addr));
  control_unit #(.applicationType("IVERILOG"), .CodeFile("./control_unit.v")) u_control_unit (
    .instr_op(opcode), .reg_dst(Regdst), .branch(u_control_unit_branch), .mem_read(mem_read),
    .mem_to_reg(memreg), .alu_op(aluop), .mem_write(mem_write), .alu_src(alusrc), .reg_write(reg_write));
  cpu_registers #(.applicationType("IVERILOG"), .CodeFile("./cpu_registers.v")) u_cpu_registers (
    .clk(clk), .rst(rst), .write_en(reg_write), .src1_addr(src1__addr), .src2_addr(src2__addr),
    .dst_addr(dst__addr), .data_in(dst__data), .src1_out(src1__out), .src2_out(src2__out));
  alu_control #(.applicationType("IVERILOG"), .CodeFile("./alu_control.v")) u_alu_control (
    .alu_op(aluop), .funct(cpumemory_d2[5:0]), .alu_control(aluc));
  alu #(.applicationType("IVERILOG"), .CodeFile("./alu.v")) u_alu_2 (
    .alu_control(4'b0010), .A(u_alu_result), .B({2'b00, bitextender_1_out[29:0]}), .result(u_alu_2_result));  // open: zero
  Multiplexer #(.Bits(32)) multiplexer_2 (
    .sel(alusrc), .in_0(src2__out), .in_1(bitextender_1_out), .out(multiplexer_2_out));
  alu #(.applicationType("IVERILOG"), .CodeFile("./alu.v")) u_alu_3 (
    .alu_control(aluc), .A(src1__out), .B(multiplexer_2_out), .zero(u_alu_3_zero),
    .result({u_alu_3_result, Alures}));
  and and_1 (and_1_out, u_control_unit_branch, u_alu_3_zero);
  Multiplexer #(.Bits(32)) multiplexer_3 (
    .sel(and_1_out), .in_0(u_alu_result), .in_1(u_alu_2_result), .out(multiplexer_3_out));
  Multiplexer #(.Bits(32)) multiplexer_4 (.sel(memreg), .in_0({u_alu_3_result, Alures}), .in_1(_1D), .out(dst__data));

  // Other names for the same wires on the sheet: src2addr[4:0] = src2__addr; src1addr[4:0] = src1__addr;
  //   data_out[31:0] = PC; dstaddr[4:0] = dst__addr; dstdata[31:0] = dst__data; src1out[31:0] = src1__out;
  //   src2out[31:0] = src2__out; src_out2[31:0] = src2__out

  // Notes on the sheet:
  //   Inputs
  //   PC
  //   Outputs for testing
endmodule
